# Fritzing sketch VectorPlotter (saved by Fritzing 1.0.3b)
breadboards: 1

parts:
  Part1 = Arduino Uno (Rev3) - ICSP
  J1 = Basic Servo [part_number=servoo mpn=ss]
  Power_plug1 = Power plug
  U1 = mystery part, 10 pins [chip_label="DM320T Stepper Driver"]
  M3 = Stepper Motor - Bipolar
  M4 = Stepper Motor - Bipolar
  U3 = mystery part, 10 pins [chip_label="DM320T Stepper Driver"]

nets:
  N1: Part1.ICSP_MOSI, Part1.D11_PWM/MOSI, J1.pulse
  5V: Part1.5V, J1.vcc, U1.pin8, U3.pin8
  N2: Part1.D2, U1.pin10
  N3: Part1.D3_PWM, U1.pin9
  N4: Part1.D6_PWM, U3.pin10
  N5: Part1.D7, U3.pin9
  GND: Part1.GND, J1.gnd
  N6: Power_plug1.GND, U1.pin6, U3.pin6
  N7: Power_plug1.VCC, U1.pin5, U3.pin5
  N8: U1.pin1, M3.A
  N9: U1.pin2, M3.B
  N10: U1.pin3, M3.C
  N11: U1.pin4, M3.D
  N12: M4.A, U3.pin1
  N13: M4.C, U3.pin3
  N14: M4.B, U3.pin2
  N15: M4.D, U3.pin4

notes:
  12V/1.5A
  USB Connection
